# Fritzing sketch RC car (saved by Fritzing 0.9.3b)
breadboards: 1

parts:
  Part3 = Arduino Uno (Rev3)
  IC1 = L293D [package=THT]
  M1 = DC Motor
  M2 = DC Motor
  VCC1 = Battery
  C3 = Capacitor Polarized [package=nippon_f80]

nets:
  N1: Part3.D8, IC1.In_2
  N2: Part3.D9_PWM, IC1.Enable_1
  N3: Part3.GND, IC1.0V, VCC1.-, C3.-
  N4: Part3.D3_PWM, IC1.In_3
  N5: Part3.D4, IC1.In_4
  N6: Part3.D5_PWM, IC1.Enable_2
  N7: Part3.D7, IC1.In_1
  N8: Part3.5V, IC1.+V
  N9: IC1.Out_1_(_Controlled_by_Enable_1_), M2.pin_1
  N10: IC1.Out_2_(_Controlled_by_Enable_1_), M2.pin_2
  N11: IC1.Out_3_(_Controlled_by_Enable_2_), M1.pin_1
  N12: IC1.Out_4_(_Controlled_by_Enable_2_), M1.pin_2
  N13: VCC1.+, C3.+
